# Fritzing sketch OLED_BMP085 (saved by Fritzing 0.8.7b)
breadboards: 1

parts:
  Part1 = Arduino Uno (Rev3)
  BMP1 = BMP085 Breakout
  OLED1 = 128x64 Monochrom OLED Display with SPI Control

nets:
  N1: Part1.A4/SDA, BMP1.SDA
  N2: Part1.A5/SCL, BMP1.SCL
  N3: Part1.D9_PWM, OLED1.Data
  N4: Part1.D10_PWM/SS, OLED1.Clock
  N5: Part1.D11_PWM/MOSI, OLED1.SA0/DC
  N6: Part1.D12/MISO, OLED1.CS
  N7: Part1.D13/SCK, OLED1.Reset
  VIN: Part1.5V, BMP1.VIN, OLED1.Vin
  GND: Part1.GND, BMP1.GND, OLED1.GND

notes:
  Wiring schematic for Arduino OLED sketch and Bosch BMP180 (BMP085.)

custom parts:
  BMP085 Breakout: A breakout for the BMP085 barometric pressure and temperature sensor
